// Logisim project ex4.circ as structural Verilog: 7 circuits, main circuit main
module main (
  input  in_1,
  input  in_2,
  input  in_3,
  input  in_4,
  input  in_5,
  input  in_6
);

  wire clock_1_out, conversor7segmentos_1_a, conversor7segmentos_1_b, conversor7segmentos_1_c,
       conversor7segmentos_1_d, registrador3bits_1__01, registrador3bits_1__02, registrador3bits_1_o0,
       somador3bits_1_s1, somador3bits_1_s2, somador3bits_1_s3;

  somador3bits somador3bits_1 (
    .a1(in_1), .a2(in_2), .a3(in_3), .b1(in_4), .b2(in_5), .b3(in_6), .s1(somador3bits_1_s1),
    .s2(somador3bits_1_s2), .s3(somador3bits_1_s3));  // open: co
  Clock clock_1 (.out(clock_1_out));
  registrador3bits registrador3bits_1 (
    .in0(somador3bits_1_s1), .in1(somador3bits_1_s2), .in2(somador3bits_1_s3), .clk(clock_1_out),
    .o0(registrador3bits_1_o0), ._01(registrador3bits_1__01), ._02(registrador3bits_1__02));
  conversor7segmentos conversor7segmentos_1 (
    .in0(registrador3bits_1__02), .in1(registrador3bits_1__01), .in2(registrador3bits_1_o0),
    .a(conversor7segmentos_1_a), .b(conversor7segmentos_1_b), .c(conversor7segmentos_1_c),
    .d(conversor7segmentos_1_d));  // open: e
  _7_Segment_Display u_7_segment_display_1 (
    .g(conversor7segmentos_1_a), .f(conversor7segmentos_1_b), .a(conversor7segmentos_1_c),
    .b(conversor7segmentos_1_d));  // open: e, d, c, dp
endmodule

module halfadder (
  input  a0,
  input  b0,
  output \output ,
  output vai1
);

  and and_1 (vai1, a0, b0);
  xor xor_1 (\output , a0, b0);
endmodule

module fulladder (
  input  a,
  input  b,
  input  ci,
  output s,
  output co
);

  wire and_1_out, and_2_out, and_3_out;

  and and_1 (and_1_out, a, b);
  and and_2 (and_2_out, a, ci);
  and and_3 (and_3_out, ci, b);
  ExactlyOne xor_1 (.out(s), .in0(a), .in1(b), .in3(ci));
  or or_1 (co, and_1_out, and_2_out, and_3_out);
endmodule

// SOMADOR
module somador3bits (
  input  a1,
  input  a2,
  input  a3,
  input  b1,
  input  b2,
  input  b3,
  output s1,
  output s2,
  output s3,
  output co
);

  wire fa_co, ha_vai1;

  halfadder ha (.a0(a1), .b0(b1), .\output (s1), .vai1(ha_vai1));
  fulladder fa (.a(a2), .b(b2), .ci(ha_vai1), .s(s2), .co(fa_co));
  fulladder fa_2 (.a(a3), .b(b3), .ci(fa_co), .s(s3), .co(co));
endmodule

module ffd (
  input  d,
  input  CLK,
  output q,
  output nq
);

  wire nand_1_out, nand_2_out, not_1_out;

  not not_1 (not_1_out, d);
  nand nand_1 (nand_1_out, d, d, CLK);
  nand nand_2 (nand_2_out, not_1_out, CLK);
  nand nand_3 (q, nand_1_out, nand_1_out, nq);
  nand nand_4 (nq, q, nand_2_out, nand_2_out);
endmodule

// REGISTRADOR
module registrador3bits (
  input  in0,
  input  in1,
  input  in2,
  input  clk,
  output o0,
  output _01,
  output _02
);

  ffd ffd_1 (.d(in0), .q(o0), .CLK(clk));  // open: nq
  ffd ffd_2 (.d(in1), .q(_01), .CLK(clk));  // open: nq
  ffd ffd_3 (.d(in2), .q(_02), .CLK(clk));  // open: nq
endmodule

module conversor7segmentos (
  input  in0,
  input  in1,
  input  in2,
  output a,
  output b,
  output c,
  output d,
  output e
);

  wire and_1_out, and_2_out, and_3_out, and_4_out, and_5_out, and_6_out, and_7_out, and_8_out, and_9_out,
       and_10_out, and_11_out, and_12_out, and_13_out, and_14_out, and_15_out, and_16_out, not_1_out,
       not_2_out, not_3_out, not_4_out, not_5_out, not_6_out, not_7_out, not_8_out, not_9_out, not_10_out,
       or_4_out;

  not not_1 (not_1_out, in2);
  not not_2 (not_2_out, in0);
  not not_3 (not_3_out, in1);
  not not_4 (not_4_out, in0);
  not not_5 (not_5_out, in1);
  not not_6 (not_6_out, in2);
  not not_7 (not_7_out, in1);
  not not_8 (not_8_out, in2);
  not not_9 (not_9_out, in1);
  not not_10 (not_10_out, in2);
  and and_1 (and_1_out, not_4_out, in1);
  and and_2 (and_2_out, in0, not_5_out, not_5_out);
  and and_3 (and_3_out, in1, not_6_out);
  and and_4 (and_4_out, not_7_out, not_8_out);
  and and_5 (and_5_out, in0, not_9_out);
  and and_6 (and_6_out, in0, not_8_out);
  and and_7 (and_7_out, not_2_out, not_1_out, not_3_out);
  and and_8 (and_8_out, not_2_out, in1);
  and and_9 (and_9_out, in0, in1);
  and and_10 (and_10_out, in0, in2);
  and and_11 (and_11_out, not_2_out, not_3_out);
  and and_12 (and_12_out, not_3_out, not_10_out);
  and and_13 (and_13_out, not_2_out, in1);
  and and_14 (and_14_out, in2, in1);
  and and_15 (and_15_out, in1, not_10_out);
  and and_16 (and_16_out, not_2_out, not_10_out);
  or or_1 (b, and_4_out, and_5_out, and_6_out);
  or or_2 (d, and_11_out, and_12_out, and_13_out, and_14_out);
  or or_3 (e, and_15_out, and_16_out);
  or or_4 (or_4_out, and_1_out, and_2_out);
  or or_5 (c, and_7_out, and_8_out, and_9_out, and_10_out);
  or or_6 (a, or_4_out, and_3_out);
endmodule
